# Fritzing sketch capPodiumCircuit (saved by Fritzing 0.9.3b)
circuit board: 6.80156cm x 6.21595cm
breadboards: 1

parts:
  Arduino_Nano_R3 = Arduino Nano (Rev3.0)
  7805 = Voltage Regulator [package=to220-igo]
  J1 = Screw terminal - 2 pins [package=THT]
  J2 = Screw terminal - 2 pins [package=THT]
  J3 = Screw terminal - 2 pins [package=THT]
  J4 = Screw terminal - 2 pins [package=THT]
  RJ45_jack = RJ45 Jack [package=rj45-8]
  J5 = Screw terminal - 2 pins [package=THT]
  SN75HVD3082EP = IC, DIP package, 8 pins [chip_label=IC]
  R1 = Resistor [tolerance=±5% resistance=220 package=THT]
  TX = LED - 5mm [color="Red (633nm)" package="5 mm [THT]"]
  RX = LED - 5mm [color="Green (570nm)" package="5 mm [THT]"]
  R2 = Resistor [tolerance=±5% resistance=1k package=THT]
  R3 = Resistor [tolerance=±5% resistance=1k package=THT]
  J6 = Screw terminal - 2 pins [package=THT]
  J7 = Screw terminal - 2 pins [package=THT]
  9–12V_in_center_+ = Power Jack [package=power_jack_pth]

nets:
  GND: Arduino_Nano_R3.GND, 7805.GND, RJ45_jack.4, RJ45_jack.5, SN75HVD3082EP.pin5, 9–12V_in_center_+.GND
  N1: Arduino_Nano_R3.D2, J6.pin1
  N2: Arduino_Nano_R3.D3, J6.pin2
  N3: Arduino_Nano_R3.D4, J7.pin1
  N4: Arduino_Nano_R3.D5, J7.pin2
  N5: Arduino_Nano_R3.D7, SN75HVD3082EP.pin2, SN75HVD3082EP.pin3
  N6: Arduino_Nano_R3.D8, SN75HVD3082EP.pin4, RX.cathode
  N7: Arduino_Nano_R3.D9, SN75HVD3082EP.pin1, TX.cathode
  N8: Arduino_Nano_R3.D10, J1.pin2
  N9: Arduino_Nano_R3.D11/MOSI, J2.pin2
  N10: Arduino_Nano_R3.D12/MISO, J2.pin1
  N11: Arduino_Nano_R3.5V, 7805.OUT, SN75HVD3082EP.pin8, R2.Pin_1, R3.Pin_1
  N12: Arduino_Nano_R3.A7, J5.pin1
  N13: Arduino_Nano_R3.A6, J5.pin2
  N14: Arduino_Nano_R3.A5, J4.pin1
  N15: Arduino_Nano_R3.A4, J4.pin2
  N16: Arduino_Nano_R3.A3, J3.pin1
  N17: Arduino_Nano_R3.A2, J3.pin2
  N18: Arduino_Nano_R3.D13/SCK, J1.pin1
  N19: 7805.IN, 9–12V_in_center_+.PWR
  N20: RJ45_jack.7, SN75HVD3082EP.pin7, R1.Pin_1
  N21: RJ45_jack.8, SN75HVD3082EP.pin6, R1.Pin_0
  N22: TX.anode, R2.Pin_0
  N23: RX.anode, R3.Pin_0

notes:
  MISO
  MOSI
  SCLK
  A7
  A6
  SS
  A5
  A4
  A3
  A2
  <-D5
  D4->
  <-D3
  D2->
  capSign v0.1 Robert Zacharias, 2018
  github.com/robzach/capitalism-works-for-me
